# Fritzing sketch canary (saved by Fritzing 0.9.3b)

parts:
  Part1 = Arduino Nano (Rev3.0)
  Part2 = LCD1602-I2C
  W5500_Module1 = W5500 Ethernet module [package="DIP (Dual Inline) [THT]"]

nets:
  GND: Part1.GND, Part2.GND, W5500_Module1.GND
  N1: Part1.D3, W5500_Module1.INT
  N2: Part1.D9, W5500_Module1.SCLK
  N3: Part1.D10, W5500_Module1.SCS
  N4: Part1.D11/MOSI, W5500_Module1.MOSI
  N5: Part1.D12/MISO, W5500_Module1.MISO
  N6: Part1.RESET, W5500_Module1.RST
  5V: Part1.5V, Part2.VCC, W5500_Module1.5V
  N7: Part1.A5, Part2.SCL
  N8: Part1.A4, Part2.SDA
  3V3: Part1.3V3, W5500_Module1.3.3V

custom parts:
  LCD1602-I2C: A standard character display, usually with 2x16 characters. Comes in many colors with LCM1602 IIC attached.
  W5500 Ethernet module: W5500 based SPI Ethernet module for Arduino, etc.
